# Fritzing sketch Rtc_servo_alarm_connections (saved by Fritzing 0.9.3b)
breadboards: 1

parts:
  Parça1 = Arduino Uno (Rev3)
  VCC1 = 4 x AAA Battery Mount
  ZS-042_RTC1 = ZS-042 RTC Module
  J1 = Basic Servo
  Digital_Panel_Meter_Voltage_DMS-20PC_by_Murata1 = Digital Panel Meter, Voltage, DMS-20PC
  S4 = Pushbutton [package=THT]

nets:
  N1: Parça1.A4/SDA, ZS-042_RTC1.SDA
  N2: Parça1.A5/SCL, ZS-042_RTC1.SCL
  N3: Parça1.D9_PWM, J1.pulse
  GND: Parça1.GND, VCC1.-, ZS-042_RTC1.GND, J1.gnd, S4.leg1
  VIN: Parça1.VIN, ZS-042_RTC1.VCC
  N4: VCC1.+, J1.vcc, Digital_Panel_Meter_Voltage_DMS-20PC_by_Murata1.6:_#DP1
  N5: Digital_Panel_Meter_Voltage_DMS-20PC_by_Murata1.7:_Reference_In, S4.leg0

notes:
  Bendeki voltmetre 3haneli seven segment. + ve - kablosu var.Bataryaya paralel bağlanıyor.Push buton ile kullandım bu örnekte ki sürekli ölçüm yapmasın.
  MG-996R High torque servo
  push-button
  Güray Gümüş
  01.05.2019
  DS-3231 RTC modülü
